# Fritzing sketch pieman (saved by Fritzing 0.9.3b)
breadboards: 1

parts:
  S1 = Momentary Switch [package=ksa_sealed_tac_switch]
  S2 = Momentary Switch [package=ksa_sealed_tac_switch]
  S3 = Momentary Switch [package=ksa_sealed_tac_switch]
  S4 = Momentary Switch [package=ksa_sealed_tac_switch]
  LED1 = RGB LED (com. cathode, rbg) [package="5 mm [THT]"]
  Part2 = Tessel 2
  R6 = Resistor [tolerance=±5% resistance=220 package="0603 [SMD]"]
  R7 = Resistor [tolerance=±5% resistance=220 package="0603 [SMD]"]
  R8 = Resistor [tolerance=±5% resistance=220 package="0603 [SMD]"]
  R9 = Resistor [tolerance=±5% resistance=220 package="0603 [SMD]"]

nets:
  N1: S1.1, Part2.3#33, R9.Pin_0
  N2: S1.3, S2.3, S3.3, S4.3, Part2.3V3
  N3: S2.1, Part2.4#34, R8.Pin_0
  N4: S3.1, Part2.3#43, R7.Pin_0
  N5: S4.1, Part2.4#74, R6.Pin_0
  N6: LED1.red_anode, Part2.6#76
  N7: LED1.common_cathode, Part2.GND, R6.Pin_1, R7.Pin_1, R8.Pin_1, R9.Pin_1
  N8: LED1.blue_anode, Part2.5
  N9: LED1.green_anode, Part2.6#36

custom parts:
  Tessel 2: Draft version of Tessel 2
